// Digital circuit PDP8-X.dig as structural Verilog
module PDP8_X (
  input  clk
);

  wire _74238_4_p12, _74238_4_p16, _74238_5_p12, _74238_5_p16, _74238_9_p12, _74238_9_p16, _74238_10_p12,
       _74238_10_p16, AC2RAMD, AC_CK, add_1_c_o, add_2_c_o, AND, and_1_out, and_3_out, and_4_out, and_5_out,
       and_6_out, and_13_out, and_14_out, and_15_out, and_16_out, and_28_out, and_29_out, and_30_out,
       and_40_out, and_41_out, and_42_out, and_43_out, and_50_out, and_51_out, and_52_out, and_53_out,
       and_54_out, and_55_out, and_56_out, and_57_out, and_58_out, and_59_out, and_60_out, and_61_out,
       and_62_out, and_63_out, and_64_out, and_65_out, and_66_out, and_67_out, and_68_out, and_69_out,
       and_70_out, and_71_out, and_74_out, and_75_out, and_77_out, and_78_out, and_79_out, and_80_out,
       and_81_out, and_82_out, and_83_out, and_84_out, and_85_out, and_86_out, and_87_out, and_88_out,
       and_89_out, and_90_out, and_91_out, and_92_out, and_93_out, and_94_out, and_95_out, and_96_out,
       and_97_out, and_98_out, and_99_out, and_100_out, and_101_out, and_102_out, and_103_out, and_104_out,
       and_105_out, and_106_out, and_107_out, and_108_out, and_109_out, and_110_out, and_111_out,
       and_112_out, and_113_out, and_114_out, and_115_out, and_116_out, and_117_out, and_118_out,
       and_119_out, and_120_out, and_121_out, and_122_out, and_123_out, and_124_out, and_125_out,
       and_126_out, and_127_out, and_128_out, and_129_out, and_130_out, and_131_out, and_132_out,
       and_133_out, and_134_out, and_135_out, and_136_out, and_137_out, and_138_out, and_139_out,
       and_159_out, CCC_BP1, CCC_BP2, CCC_BPI, CCC_BPICTRL, CCC_H, CCC_HLTCTRL, CCC_I, CCC_R, CCC_S, CK0,
       CK1, CK2, CK3, CK4, CK5, CK6, CK7, CK8, CK9, CLA, CLA_KCC, CLAx, CLL, comparator_1_eq, counter_1_ovf,
       d_ff_1_q, d_ff_as_2_q, DATA_CK, DCA, DIRECT, DONE, driver_10_out, FLAG_GIE, FLAG_KBD, FLAG_KBDIE,
       FLAG_PRN, FORCE4000, HALT, i_cla, i_cll, i_cma, i_cml, i_hlt, i_iac, i_nop, i_osr, i_ral, i_rar,
       i_rtl, i_rtr, i_skp, i_sma, i_sna, i_snl, i_spa, i_sza, i_szl, IN_IR2PC, INC2RAMD, INCZERO, IND2INC,
       IND2PC, IND2RAMA, IND_CK, INDIRECT, INIR2RAMA, IOT, IOT_CAF, IOT_DEV5, IOT_DEV6, IOT_DEV7, IOT_DEVCPU,
       IOT_DEVHSP, IOT_DEVHSR, IOT_DEVKBD, IOT_DEVPRI, IOT_GTF, IOT_IOF, IOT_ION, IOT_KCC, IOT_KCF, IOT_KIE,
       IOT_KRB, IOT_KRS, IOT_KSF, IOT_RTF, IOT_SGT, IOT_SKON, IOT_SRQ, IOT_TCF, IOT_TFL, IOT_TLS, IOT_TPC,
       IOT_TSF, IOT_TSK, IR2PC, IR2RAMA, IR_CK, IRQ_BUS, IRQ_INHIBIT, IRQ_JMS, ISZ, JMP, JMS, KEYBOARD_av,
       L_CAF, L_DEV5, L_DEV6, L_DEV7, L_DEVCPU, L_DEVHSP, L_DEVHSR, L_DEVKBD, L_DEVPRI, LD2INC, LINK,
       LINK_CK, monoflop_1_nq, monoflop_2_q, monoflop_3_q, monoflop_4_q, MQ_CK, nor_1_out, nor_2_out,
       nor_3_out, nor_4_out, nor_5_out, nor_6_out, nor_7_out, nor_8_out, not_1_out, not_2_out, not_3_out,
       not_4_out, not_5_out, not_6_out, not_7_out, not_9_out, not_10_out, not_11_out, not_12_out, not_13_out,
       not_14_out, OPR1, OPR2, OPR3, OPR_CLL, OPR_CMA, OPR_CML, OPR_HLT, OPR_IAC, OPR_LEFT, OPR_NA1, OPR_O,
       OPR_OSR, OPR_RIGHT, OPR_SMASPA, OPR_SNLSZL, OPR_SZASNA, OPR_TSTINV, OPR_X2, or_1_out, or_2_out,
       or_4_out, or_5_out, or_6_out, or_7_out, or_9_out, or_10_out, or_11_out, or_12_out, or_13_out,
       or_14_out, or_15_out, or_16_out, or_18_out, or_19_out, or_20_out, or_21_out, or_22_out, OR_KBD12,
       OR_STATUS12, PC2ADDR, PC2RAMD, PC_CK, PC_eq_200, PC_LD, PH_FIRST, PH_LAST, PH_STB, RAM_OE, RAMA_HOLD,
       RAMD2AC_ADD, RAMD2AC_AND, RAMD2IND, RAMD2PC, ramspy_1_o, ramspy_2_o, reset_1_out, ROT2AC,
       rotater_1_p5, rs_ff_as_1_q, rs_ff_as_2_q, RTF_IOF, RTF_ION, RTF_LINK, SKIP, STB0, STB1, STB2, STB3,
       STB4, STB5, STB6, STB7, STB8, STB9, TAD_OVF_q, xor_1_out, xor_3_out, xor_4_out, xor_5_out, xor_6_out;
  wire [3:0] CK_NUM;
  wire [4:0] add_3_s, counter_1_out, multiplexer_1_out;
  wire [5:0] L_KBD, L_PRN;
  wire [7:1] L_CPU;
  wire [8:8] L_OPR1;
  wire [9:9] L_OPR2;
  wire [10:0] L_GEN;
  wire [11:0] AC, add_1_s, add_2_s, and_2_out, and_7_out, and_12_out, autospy_1__10, autospy_1__11,
       autospy_1__12, autospy_1__13, autospy_1__14, autospy_1__15, autospy_1__16, autospy_1__17,
       bitextender_1_out, bitextender_2_out, bitextender_3_out, BUS_IR, BUS_PC, DATA, dipswitch_1_out,
       driver_1_out, driver_4_out, driver_22_out, INC_s, INDOUT, KBD12, LATCHED_PC, LATCHEDDATA, MQ,
       not_8_out, or_3_out, PCIN, rotater_1_p4, xor_2_out;
  wire [12:0] L_OPR3;
  wire [15:0] KEYBOARD_d;
  wire [24:0] DAW;
  wire [31:0] INSTCNT;

  // Probe on BUS_IR
  nor nor_1 (nor_1_out, BUS_IR[4], BUS_IR[5], BUS_IR[6]);
  nor nor_2 (nor_2_out, LATCHED_PC[7], LATCHED_PC[8], LATCHED_PC[9]);
  nor nor_3 (nor_3_out, LATCHED_PC[10], LATCHED_PC[11], 1'b0);
  and and_1 (and_1_out, BUS_IR[3], nor_1_out);
  Seven_Seg_Hex seven_seg_hex_1 (.d({1'b0, BUS_PC[11:9]}), .dp(1'b0));
  Seven_Seg_Hex seven_seg_hex_2 (.d({1'b0, BUS_IR[11:9]}), .dp(1'b0));
  Seven_Seg_Hex seven_seg_hex_3 (.d({1'b0, AC[11:9]}), .dp(1'b0));
  Seven_Seg_Hex seven_seg_hex_4 (.d({1'b0, MQ[11:9]}), .dp(1'b0));
  LED led_1 (.in(LINK));
  RAMSPY ramspy_1 (.A(12'h12), .O(ramspy_1_o), .DAW(DAW));
  RAMSPY ramspy_2 (.A(12'h7e7), .O(ramspy_2_o), .DAW(DAW));
  AUTOSPY autospy_1 (
    .DAW(DAW), ._10(autospy_1__10), ._11(autospy_1__11), ._12(autospy_1__12), ._13(autospy_1__13),
    ._14(autospy_1__14), ._15(autospy_1__15), ._16(autospy_1__16), ._17(autospy_1__17));
  // Probe on DATA
  not not_1 (not_1_out, BUS_IR[7]);
  // _74238 _74238_1: pin names not known; wires that end beside it: 1'b1, 1'b0, 1'b1, 1'b0, 1'b0, BUS_IR[9], BUS_IR[10], BUS_IR[11], AND, L_GEN[10], ISZ, DCA, JMS, JMP, IOT, L_GEN[4]
  Seven_Seg_Hex seven_seg_hex_5 (.d({1'b0, BUS_PC[8:6]}), .dp(1'b0));
  Seven_Seg_Hex seven_seg_hex_6 (.d({1'b0, BUS_IR[8:6]}), .dp(1'b0));
  Seven_Seg_Hex seven_seg_hex_7 (.d({1'b0, AC[8:6]}), .dp(1'b0));
  Seven_Seg_Hex seven_seg_hex_8 (.d({1'b0, MQ[8:6]}), .dp(1'b0));
  assign and_2_out = AC & DATA;  // And and_2, 12 bits wide
  Add #(.Bits(12)) add_1 (.a(AC), .b(DATA), .c_i(1'b0), .s(add_1_s), .c_o(add_1_c_o));
  and and_3 (and_3_out, add_1_c_o, RAMD2AC_ADD);
  LED led_2 (.in(RAMD2AC_ADD));
  and and_4 (and_4_out, nor_2_out, nor_3_out, and_1_out);
  and and_5 (and_5_out, not_1_out, and_1_out);
  Seven_Seg_Hex seven_seg_hex_9 (.d({1'b0, BUS_PC[5:3]}), .dp(1'b0));
  Seven_Seg_Hex seven_seg_hex_10 (.d({1'b0, BUS_IR[5:3]}), .dp(1'b0));
  Seven_Seg_Hex seven_seg_hex_11 (.d({1'b0, AC[5:3]}), .dp(1'b0));
  Seven_Seg_Hex seven_seg_hex_12 (.d({1'b0, MQ[5:3]}), .dp(1'b0));
  // Probe on ramspy_1_o
  // Probe on ramspy_2_o
  // Probe on autospy_1__10
  // Probe on autospy_1__11
  // Probe on autospy_1__12
  // Probe on autospy_1__13
  // Probe on autospy_1__14
  // Probe on autospy_1__15
  // Probe on autospy_1__16
  // Probe on autospy_1__17
  LED led_3 (.in(add_1_c_o));
  LED led_4 (.in(and_3_out));
  LED led_5 (.in(STB4));
  not not_2 (not_2_out, 1'b0);
  not not_3 (not_3_out, 1'b0);
  not not_4 (not_4_out, 1'b0);
  Seven_Seg_Hex seven_seg_hex_13 (.d({1'b0, BUS_PC[2:0]}), .dp(1'b0));
  Seven_Seg_Hex seven_seg_hex_14 (.d({1'b0, BUS_IR[2:0]}), .dp(1'b0));
  Seven_Seg_Hex seven_seg_hex_15 (.d({1'b0, AC[2:0]}), .dp(1'b0));
  Seven_Seg_Hex seven_seg_hex_16 (.d({1'b0, MQ[2:0]}), .dp(1'b0));
  // Probe on AC
  // Probe on and_2_out
  // Probe on add_1_s
  // Probe on rotater_1_p4
  D_FF TAD_OVF (.D(and_3_out), .C(STB4), .Q(TAD_OVF_q));  // open: nQ
  nor nor_4 (nor_4_out, and_4_out, 1'b0, and_5_out);
  nor nor_5 (nor_5_out, not_2_out, not_3_out, not_4_out);
  LED led_6 (.in(MQ_CK));
  LED led_7 (.in(TAD_OVF_q));
  LED led_8 (.in(L_OPR3[12]));
  LED led_9 (.in(L_OPR2[9]));
  LED led_10 (.in(i_nop));
  LED led_11 (.in(AND));
  LED led_12 (.in(AC[11]));
  LED led_13 (.in(MQ[11]));
  and and_6 (and_6_out, L_OPR3[7], MQ_CK);
  assign driver_1_out = RAMD2AC_AND ? and_2_out : 12'bz;  // Driver driver_1
  LED led_14 (.in(RAMD2AC_AND));
  assign driver_1_out = RAMD2AC_ADD ? add_1_s : 12'bz;  // Driver driver_2
  LED led_15 (.in(RAMD2AC_ADD));
  assign driver_1_out = ROT2AC ? rotater_1_p4 : 12'bz;  // Driver driver_3
  LED led_16 (.in(ROT2AC));
  xor xor_1 (xor_1_out, TAD_OVF_q, rotater_1_p5);
  not not_5 (not_5_out, nor_4_out);
  not not_6 (not_6_out, BUS_IR[8]);
  LED led_17 (.in(L_OPR3[11]));
  LED led_18 (.in(i_skp));
  LED led_19 (.in(L_OPR1[8]));
  LED led_20 (.in(L_GEN[10]));
  LED led_21 (.in(AC[10]));
  LED led_22 (.in(AC[9]));
  LED led_23 (.in(MQ[10]));
  LED led_24 (.in(MQ[9]));
  Seven_Seg_Hex seven_seg_hex_17 (.d(CK_NUM), .dp(1'b0));
  // Probe on and_7_out
  LED led_25 (.in(and_6_out));
  // Probe on driver_1_out
  LED led_26 (.in(xor_1_out));
  nor nor_6 (nor_6_out, L_GEN[4], 1'b0, IOT);
  LED led_27 (.in(L_OPR3[10]));
  LED led_28 (.in(i_sma));
  LED led_29 (.in(i_cll));
  LED led_30 (.in(ISZ));
  LED led_31 (.in(AC[8]));
  LED led_32 (.in(AC[7]));
  LED led_33 (.in(MQ[8]));
  LED led_34 (.in(MQ[7]));
  // Probe on LATCHED_PC
  Counter #(.Bits(32)) INSTRUCTION_COUNT (.en(1'b1), .C(CK0), .clr(1'b0), .out(INSTCNT));  // open: ovf
  assign and_7_out = AC & ~bitextender_1_out;  // And and_7, 12 bits wide
  D_FF #(.Bits(12)) u_AC (.D(driver_1_out), .C(AC_CK), .Q(AC));  // open: nQ
  LED led_35 (.in(AC_CK));
  D_FF u_LINK (.D(xor_1_out), .C(LINK_CK), .Q(LINK));  // open: nQ
  LED led_36 (.in(LINK_CK));
  and and_8 (L_GEN[1], nor_6_out, BUS_IR[8], not_5_out);
  and and_9 (INDIRECT, nor_6_out, BUS_IR[8], nor_4_out);
  and and_10 (DIRECT, nor_6_out, not_6_out);
  and and_11 (L_GEN[0], nor_6_out, BUS_IR[7]);
  LED led_37 (.in(L_OPR3[9]));
  LED led_38 (.in(L_OPR3[8]));
  LED led_39 (.in(i_sza));
  LED led_40 (.in(i_spa));
  LED led_41 (.in(i_cma));
  LED led_42 (.in(i_cml));
  LED led_43 (.in(DCA));
  LED led_44 (.in(JMS));
  LED led_45 (.in(AC[6]));
  LED led_46 (.in(AC[5]));
  LED led_47 (.in(MQ[6]));
  LED led_48 (.in(MQ[5]));
  LED led_49 (.in(PH_FIRST));
  LED led_50 (.in(PH_STB));
  // Probe COUNT on INSTCNT
  D_FF #(.Bits(12)) u_MQ (.D(and_7_out), .C(and_6_out), .Q(MQ));  // open: nQ
  or or_1 (or_1_out, L_OPR1[8], L_OPR2[9], L_OPR3[11], L_OPR3[7], CLA, CLA_KCC);
  LED led_51 (.in(or_1_out));
  LED led_52 (.in(LINK));
  LED led_53 (.in(L_GEN[1]));
  LED led_54 (.in(INDIRECT));
  LED led_55 (.in(DIRECT));
  LED led_56 (.in(L_GEN[0]));
  LED led_57 (.in(L_OPR3[7]));
  LED led_58 (.in(i_sna));
  LED led_59 (.in(i_iac));
  LED led_60 (.in(JMP));
  LED led_61 (.in(AC[4]));
  LED led_62 (.in(AC[3]));
  LED led_63 (.in(MQ[4]));
  LED led_64 (.in(MQ[3]));
  LED led_65 (.in(PH_LAST));
  // Probe MQ on MQ
  BitExtender #(.inputBits(1), .outputBits(12)) bitextender_1 (.in(L_OPR3[11]), .out(bitextender_1_out));
  // Probe AC on AC
  BitExtender #(.inputBits(1), .outputBits(12)) bitextender_2 (.in(or_1_out), .out(bitextender_2_out));
  // Probe LINK on LINK
  LED led_66 (.in(OPR_CLL));
  LED led_67 (.in(L_OPR3[6]));
  LED led_68 (.in(i_snl));
  LED led_69 (.in(i_rar));
  LED led_70 (.in(IOT));
  LED led_71 (.in(AC[2]));
  LED led_72 (.in(AC[1]));
  LED led_73 (.in(MQ[2]));
  LED led_74 (.in(MQ[1]));
  assign and_12_out = AC & ~bitextender_2_out;  // And and_12, 12 bits wide
  or or_2 (or_2_out, CLL, OPR_CLL);
  LED led_75 (.in(L_OPR3[5]));
  LED led_76 (.in(L_OPR3[4]));
  LED led_77 (.in(i_szl));
  LED led_78 (.in(i_osr));
  LED led_79 (.in(i_rtr));
  LED led_80 (.in(i_ral));
  LED led_81 (.in(L_GEN[4]));
  LED led_82 (.in(DIRECT));
  LED led_83 (.in(AC[0]));
  LED led_84 (.in(MQ[0]));
  assign driver_4_out = L_OPR3[8] ? MQ : 12'bz;  // Driver driver_4
  LED led_85 (.in(L_OPR3[8]));
  // Probe on and_12_out
  and and_13 (and_13_out, LINK, ~or_2_out);  // And
  LED led_86 (.in(L_OPR3[3]));
  LED led_87 (.in(i_hlt));
  LED led_88 (.in(i_rtl));
  LED led_89 (.in(INDIRECT));
  assign or_3_out = driver_4_out | and_12_out;  // Or or_3, 12 bits wide
  LED led_90 (.in(and_13_out));
  LED led_91 (.in(OPR_CML));
  LED led_92 (.in(IOT));
  and and_14 (and_14_out, IOT, CK6);
  LED led_93 (.in(L_OPR3[2]));
  LED led_94 (.in(L_GEN[1]));
  // Probe on {LINK, 1'b0, IRQ_BUS, IRQ_INHIBIT, FLAG_GIE, {7{1'b0}}}
  assign driver_4_out = OR_STATUS12 ? {LINK, 1'b0, IRQ_BUS, IRQ_INHIBIT, FLAG_GIE, {7{1'b0}}} : 12'bz;  // Driver driver_5
  LED led_95 (.in(OR_STATUS12));
  // Probe on KBD12
  assign driver_4_out = OR_KBD12 ? KBD12 : 12'bz;  // Driver driver_6
  LED led_96 (.in(OR_KBD12));
  // Probe on not_8_out
  assign driver_4_out = OPR_OSR ? not_8_out : 12'bz;  // Driver driver_7
  LED led_97 (.in(OPR_OSR));
  // Probe on driver_4_out
  // Probe on or_3_out
  BitExtender #(.inputBits(1), .outputBits(12)) bitextender_3 (.in(OPR_CMA), .out(bitextender_3_out));
  LED led_98 (.in(OPR_CMA));
  or or_4 (or_4_out, RTF_LINK, OPR_CML);
  and and_15 (and_15_out, not_7_out, IOT);
  not not_7 (not_7_out, CK0);
  or or_5 (or_5_out, BUS_IR[8], BUS_IR[7], BUS_IR[6]);
  LED led_99 (.in(and_14_out));
  LED led_100 (.in(L_OPR3[1]));
  LED led_101 (.in(L_OPR3[0]));
  LED led_102 (.in(L_GEN[0]));
  Button S (.out(CCC_S));
  Button I (.out(CCC_I));
  Button R (.out(CCC_R));
  Button H (.out(CCC_H));
  Button P (.out(PC_eq_200));
  assign xor_2_out = or_3_out ^ bitextender_3_out;  // XOr xor_2, 12 bits wide
  xor xor_3 (xor_3_out, and_13_out, or_4_out);
  assign DONE = and_14_out ? and_14_out : 1'bz;  // Driver driver_8
  // Probe on xor_2_out
  LED led_103 (.in(xor_3_out));
  LED led_104 (.in(L_PRN[5]));
  LED led_105 (.in(L_KBD[5]));
  LED led_106 (.in(L_CPU[7]));
  LED led_107 (.in(FLAG_GIE));
  DipSwitch #(.dipDefault("true")) dipswitch_1 (.out(dipswitch_1_out[11]));
  DipSwitch #(.dipDefault("true")) dipswitch_2 (.out(dipswitch_1_out[10]));
  assign not_8_out = ~dipswitch_1_out;  // Not not_8, 12 bits wide
  LED led_108 (.in(OPR_IAC));
  xor xor_4 (xor_4_out, and_16_out, xor_3_out);
  // _74238 _74238_2: pin names not known; wires that end beside it: 1'b1, 1'b0, and_15_out, 1'b0, or_5_out, BUS_IR[3], BUS_IR[4], BUS_IR[5], IOT_DEVCPU, IOT_DEVHSR, IOT_DEVHSP, IOT_DEVKBD, IOT_DEVPRI, IOT_DEV5, IOT_DEV6, IOT_DEV7
  LED led_109 (.in(L_PRN[4]));
  LED led_110 (.in(L_KBD[4]));
  LED led_111 (.in(L_CPU[6]));
  LED led_112 (.in(IRQ_BUS));
  Switch #(.Closed("true")) ENABLE (.A(HALT), .B(CCC_HLTCTRL));
  Switch #(.Closed("true")) ENABLE_2 (.A(CCC_BP1), .B(CCC_BP2));
  Switch ENABLE_3 (.A(CCC_BPI), .B(CCC_BPICTRL));
  DipSwitch #(.dipDefault("true")) dipswitch_3 (.out(dipswitch_1_out[9]));
  DipSwitch #(.dipDefault("true")) dipswitch_4 (.out(dipswitch_1_out[8]));
  DipSwitch #(.dipDefault("true")) dipswitch_5 (.out(dipswitch_1_out[7]));
  Add #(.Bits(12)) add_2 (.a(xor_2_out), .b({12{1'b0}}), .c_i(OPR_IAC), .s(add_2_s), .c_o(add_2_c_o));
  LED led_113 (.in(xor_4_out));
  LED led_114 (.in(L_PRN[3]));
  LED led_115 (.in(L_KBD[3]));
  LED led_116 (.in(L_CPU[5]));
  LED led_117 (.in(FLAG_KBDIE));
  Switch KILL (.A(CCC_HLTCTRL), .B(1'b0));
  Switch KILL_2 (.A(CCC_BPICTRL), .B(1'b0));
  DipSwitch #(.dipDefault("true")) dipswitch_6 (.out(dipswitch_1_out[6]));
  DipSwitch #(.dipDefault("true")) dipswitch_7 (.out(dipswitch_1_out[5]));
  DipSwitch #(.dipDefault("true")) dipswitch_8 (.out(dipswitch_1_out[4]));
  // Probe on add_2_s
  and and_16 (and_16_out, add_2_c_o, OPR_IAC);
  LED led_118 (.in(add_2_c_o));
  LED led_119 (.in(L_PRN[2]));
  LED led_120 (.in(L_PRN[1]));
  LED led_121 (.in(L_KBD[2]));
  LED led_122 (.in(L_KBD[1]));
  LED led_123 (.in(L_CPU[4]));
  LED led_124 (.in(L_CPU[3]));
  LED led_125 (.in(FLAG_KBD));
  LED led_126 (.in(FLAG_PRN));
  // Probe on INSTCNT
  DipSwitch #(.dipDefault("true")) dipswitch_9 (.out(dipswitch_1_out[3]));
  DipSwitch #(.dipDefault("true")) dipswitch_10 (.out(dipswitch_1_out[2]));
  DipSwitch #(.dipDefault("true")) dipswitch_11 (.out(dipswitch_1_out[1]));
  LED led_127 (.in(and_16_out));
  // _74238 _74238_3: pin names not known; wires that end beside it: 1'b1, 1'b0, IOT_DEVCPU, 1'b0, 1'b0, BUS_IR[0], BUS_IR[1], BUS_IR[2], IOT_SKON, IOT_ION, IOT_IOF, IOT_SRQ, IOT_GTF, IOT_RTF, IOT_SGT, IOT_CAF
  // _74238 _74238_4: pin names not known; wires that end beside it: 1'b1, 1'b0, IOT_DEVKBD, 1'b0, 1'b0, BUS_IR[0], BUS_IR[1], BUS_IR[2], IOT_KCF, IOT_KSF, IOT_KCC, _74238_4_p12, IOT_KRS, IOT_KIE, IOT_KRB, _74238_4_p16, _74238_4_p12, _74238_4_p16
  // _74238 _74238_5: pin names not known; wires that end beside it: 1'b1, 1'b0, IOT_DEVPRI, 1'b0, 1'b0, BUS_IR[0], BUS_IR[1], BUS_IR[2], IOT_TFL, IOT_TSF, IOT_TCF, _74238_5_p12, IOT_TPC, IOT_TSK, IOT_TLS, _74238_5_p16, _74238_5_p12, _74238_5_p16
  LED led_128 (.in(L_PRN[0]));
  LED led_129 (.in(L_KBD[0]));
  LED led_130 (.in(L_CPU[2]));
  DipSwitch #(.dipDefault("true")) dipswitch_12 (.out(dipswitch_1_out[0]));
  LED led_131 (.in(L_CPU[1]));
  Seven_Seg_Hex seven_seg_hex_18 (.d(CK_NUM), .dp(1'b0));
  // ROTATER rotater_1: pin names not known; wires that end beside it: {OPR_RIGHT, OPR_LEFT, OPR_X2}, add_2_s, xor_4_out, rotater_1_p4, rotater_1_p5
  LED led_132 (.in(L_CAF));
  // Probe on LATCHED_PC
  LED led_133 (.in(PH_FIRST));
  // Probe on rotater_1_p4
  LED led_134 (.in(PH_STB));
  LED led_135 (.in(PH_LAST));
  LED led_136 (.in(L_GEN[4]));
  not not_9 (not_9_out, BUS_IR[8]);
  not not_10 (not_10_out, BUS_IR[0]);
  assign PCIN = PC_eq_200 ? 12'h80 : 12'bz;  // Driver driver_9
  assign driver_10_out = PC_eq_200 ? PC_eq_200 : 1'bz;  // Driver driver_10
  assign PC_LD = PC_eq_200 ? PC_eq_200 : 1'bz;  // Driver driver_11
  and and_17 (OPR1, not_9_out, 1'b1, L_GEN[4]);
  LED led_137 (.in(OPR1));
  and and_18 (OPR2, not_10_out, BUS_IR[8], L_GEN[4]);
  LED led_138 (.in(OPR2));
  and and_19 (OPR3, BUS_IR[8], BUS_IR[0], L_GEN[4]);
  LED led_139 (.in(OPR3));
  // OC12 oc12_1: pin names not known; wires that end beside it: BUS_IR[6:0], LATCHED_PC[11:7], L_GEN[0], IR2PC, PCIN[6:0], PCIN[11:7], PCIN
  LED led_140 (.in(IR2PC));
  // Probe PCIN on PCIN
  LED led_141 (.in(PC_CK));
  xor xor_5 (xor_5_out, PC_CK, driver_10_out);
  LED led_142 (.in(RAMD2PC));
  assign PCIN = RAMD2PC ? DATA : 12'bz;  // Driver driver_12
  LED led_143 (.in(IND2PC));
  assign PCIN = IND2PC ? INDOUT : 12'bz;  // Driver driver_13
  and and_20 (OPR_IAC, BUS_IR[0], OPR1);
  and and_21 (OPR_X2, BUS_IR[1], OPR1);
  and and_22 (OPR_LEFT, BUS_IR[2], OPR1);
  and and_23 (OPR_RIGHT, BUS_IR[3], OPR1);
  and and_24 (OPR_CML, BUS_IR[4], OPR1);
  and and_25 (OPR_CMA, BUS_IR[5], OPR1);
  and and_26 (OPR_CLL, BUS_IR[6], OPR1);
  and and_27 (L_OPR1[8], BUS_IR[7], OPR1);
  LED led_144 (.in(OPR1));
  xor xor_6 (xor_6_out, CK0, PC_eq_200);
  not not_11 (not_11_out, xor_5_out);
  nor nor_7 (nor_7_out, AC[0], AC[1], AC[2], AC[3], AC[4], AC[5], AC[6], AC[7], AC[8], AC[9], AC[10], AC[11]);
  LED led_145 (.in(nor_7_out));
  LED led_146 (.in(OPR_IAC));
  LED led_147 (.in(OPR_X2));
  LED led_148 (.in(OPR_LEFT));
  LED led_149 (.in(OPR_RIGHT));
  LED led_150 (.in(OPR_CML));
  LED led_151 (.in(OPR_CMA));
  LED led_152 (.in(OPR_CLL));
  LED led_153 (.in(L_OPR1[8]));
  CounterPreset #(.Bits(12)) PC (
    .en(1'b1), .C(not_11_out), .dir(1'b0), .in(PCIN), .ld(PC_LD), .clr(reset_1_out), .out(BUS_PC));  // open: ovf
  LED led_154 (.in(PC_LD));
  Register #(.Bits(12)) register_1 (.D(BUS_PC), .C(xor_6_out), .en(1'b1), .Q(LATCHED_PC));
  Reset #(.invertOutput("false")) reset_1 (.out(reset_1_out));
  and and_28 (and_28_out, nor_7_out, OPR_SZASNA);
  LED led_155 (.in(and_28_out));
  and and_29 (and_29_out, AC[11], OPR_SMASPA);
  LED led_156 (.in(and_29_out));
  and and_30 (and_30_out, LINK, OPR_SNLSZL);
  LED led_157 (.in(and_30_out));
  // Probe PCOUT on BUS_PC
  or or_6 (or_6_out, and_28_out, and_29_out, and_30_out);
  // Probe PCLATCHED on LATCHED_PC
  // OC12 oc12_2: pin names not known; wires that end beside it: BUS_PC, BUS_IR[6:0], LATCHED_PC[11:7], L_GEN[0], IR2RAMA, DAW[18:12], DAW[23:19]
  LED led_158 (.in(IR2RAMA));
  LED led_159 (.in(or_6_out));
  and and_31 (OPR_NA1, BUS_IR[0], OPR2);
  and and_32 (OPR_HLT, BUS_IR[1], OPR2);
  and and_33 (OPR_OSR, BUS_IR[2], OPR2);
  and and_34 (OPR_TSTINV, BUS_IR[3], OPR2);
  and and_35 (OPR_SNLSZL, BUS_IR[4], OPR2);
  and and_36 (OPR_SZASNA, BUS_IR[5], OPR2);
  and and_37 (OPR_SMASPA, BUS_IR[6], OPR2);
  and and_38 (L_OPR2[9], BUS_IR[7], OPR2);
  LED led_160 (.in(OPR2));
  LED led_161 (.in(PC2ADDR));
  assign DAW[23:12] = PC2ADDR ? BUS_PC : 12'bz;  // Driver driver_14
  xor xor_7 (SKIP, or_6_out, OPR_TSTINV);
  LED led_162 (.in(SKIP));
  and and_39 (HALT, OPR_HLT, CK4);
  LED led_163 (.in(HALT));
  LED led_164 (.in(OPR_NA1));
  LED led_165 (.in(OPR_HLT));
  LED led_166 (.in(OPR_OSR));
  LED led_167 (.in(OPR_TSTINV));
  LED led_168 (.in(OPR_SNLSZL));
  LED led_169 (.in(OPR_SZASNA));
  LED led_170 (.in(OPR_SMASPA));
  LED led_171 (.in(L_OPR2[9]));
  // Probe RAMA on DAW[23:12]
  LED led_172 (.in(DAW[24]));
  LED led_173 (.in(RAM_OE));
  LED led_174 (.in(IND2RAMA));
  assign DAW[23:12] = IND2RAMA ? INDOUT : 12'bz;  // Driver driver_15
  EEPROM #(.AddrBits(17), .isProgramMemory("true"), .Bits(12)) eeprom_1 (
    .A({5'b01100, DAW[23:12]}), .CS(1'b1), .WE(DAW[24]), .OE(RAM_OE), .D(DAW[11:0]));
  // Probe RAMD on DAW[11:0]
  LED led_175 (.in(OPR3));
  assign DATA = RAM_OE ? DAW[11:0] : 12'bz;  // Driver driver_16
  assign DAW[11:0] = DAW[24] ? DATA : 12'bz;  // Driver driver_17
  nor nor_8 (nor_8_out, BUS_IR[0], BUS_IR[1], BUS_IR[2], BUS_IR[3], BUS_IR[4], BUS_IR[5], BUS_IR[6], BUS_IR[7]);
  and and_40 (and_40_out, OPR3, BUS_IR[0]);
  LED led_176 (.in(and_40_out));
  and and_41 (and_41_out, OPR3, BUS_IR[1]);
  LED led_177 (.in(and_41_out));
  and and_42 (and_42_out, OPR3, BUS_IR[2]);
  LED led_178 (.in(and_42_out));
  and and_43 (and_43_out, OPR3, BUS_IR[3]);
  LED led_179 (.in(and_43_out));
  and and_44 (L_OPR3[7], OPR3, BUS_IR[4]);
  LED led_180 (.in(L_OPR3[7]));
  and and_45 (L_OPR3[10], OPR3, BUS_IR[5]);
  LED led_181 (.in(L_OPR3[10]));
  and and_46 (L_OPR3[8], OPR3, BUS_IR[6]);
  LED led_182 (.in(L_OPR3[8]));
  and and_47 (L_OPR3[11], OPR3, BUS_IR[7]);
  LED led_183 (.in(L_OPR3[11]));
  LED led_184 (.in(FORCE4000));
  assign DATA = FORCE4000 ? 12'h800 : 12'bz;  // Driver driver_18
  LED led_185 (.in(PC2RAMD));
  assign DATA = PC2RAMD ? BUS_PC : 12'bz;  // Driver driver_19
  // Probe DATA on DATA
  LED led_186 (.in(AC2RAMD));
  assign DATA = AC2RAMD ? AC : 12'bz;  // Driver driver_20
  and and_48 (L_OPR3[12], nor_8_out, L_GEN[4]);
  and and_49 (L_OPR3[9], L_OPR3[7], L_OPR3[8]);
  not not_12 (not_12_out, IR_CK);
  LED led_187 (.in(IR_CK));
  LED led_188 (.in(INC2RAMD));
  assign DATA = INC2RAMD ? INC_s : 12'bz;  // Driver driver_21
  LED led_189 (.in(L_OPR3[12]));
  // _74238 _74238_6: pin names not known; wires that end beside it: and_40_out, 1'b1, 1'b0, 1'b1, 1'b0, 1'b0, and_41_out, and_42_out, and_43_out, OPR_O, L_OPR3[0], L_OPR3[1], L_OPR3[2], L_OPR3[3], L_OPR3[4], L_OPR3[5], L_OPR3[6]
  LED led_190 (.in(L_OPR3[9]));
  // TRANSP_LATCH IR: pin names not known; wires that end beside it: DATA, DATA, not_12_out, BUS_IR, BUS_IR
  // Probe IR on BUS_IR
  D_FF #(.Bits(12)) IND (.D(DATA), .C(IND_CK), .Q(INDOUT));  // open: nQ
  LED led_191 (.in(IND_CK));
  LED led_192 (.in(OPR_O));
  LED led_193 (.in(L_OPR3[0]));
  LED led_194 (.in(L_OPR3[1]));
  LED led_195 (.in(L_OPR3[2]));
  LED led_196 (.in(L_OPR3[3]));
  LED led_197 (.in(L_OPR3[4]));
  LED led_198 (.in(L_OPR3[5]));
  LED led_199 (.in(L_OPR3[6]));
  // Probe INDOUT on INDOUT
  D_FF #(.Bits(12)) DATA_2 (.D(DATA), .C(DATA_CK), .Q(LATCHEDDATA));  // open: nQ
  LED led_200 (.in(DATA_CK));
  // Probe LATDATA on LATCHEDDATA
  LED led_201 (.in(IND2INC));
  assign driver_22_out = IND2INC ? INDOUT : 12'bz;  // Driver driver_22
  LED led_202 (.in(LD2INC));
  assign driver_22_out = LD2INC ? LATCHEDDATA : 12'bz;  // Driver driver_23
  or or_7 (or_7_out, IOT_ION, RTF_ION);
  and and_50 (and_50_out, FLAG_KBDIE, FLAG_KBD);
  Seven_Seg_Hex seven_seg_hex_19 (.d(CK_NUM), .dp(1'b0));
  LED led_203 (.in(PH_FIRST));
  LED led_204 (.in(PH_STB));
  // Probe AFTERINC on INC_s
  // Probe TOINC on driver_22_out
  and and_51 (and_51_out, CK4, or_7_out);
  LED led_205 (.in(or_7_out));
  and and_52 (and_52_out, IOT_CAF, CK4);
  LED led_206 (.in(and_52_out));
  and and_53 (and_53_out, IOT_CAF, STB4);
  LED led_207 (.in(and_53_out));
  and and_54 (and_54_out, IOT_SKON, FLAG_GIE, CK4);
  LED led_208 (.in(and_54_out));
  and and_55 (and_55_out, IOT_SKON, FLAG_GIE, STB4);
  LED led_209 (.in(and_55_out));
  LED led_210 (.in(and_50_out));
  LED led_211 (.in(PH_LAST));
  Add #(.Bits(12)) INC (.a({12{1'b0}}), .b(driver_22_out), .c_i(1'b1), .s(INC_s), .c_o(INCZERO));
  LED led_212 (.in(and_51_out));
  assign CLL = and_52_out ? and_52_out : 1'bz;  // Driver driver_24
  assign CLA = and_52_out ? and_52_out : 1'bz;  // Driver driver_25
  assign ROT2AC = and_52_out ? and_52_out : 1'bz;  // Driver driver_26
  assign AC_CK = and_53_out ? and_53_out : 1'bz;  // Driver driver_27
  assign LINK_CK = and_53_out ? and_53_out : 1'bz;  // Driver driver_28
  assign PC_CK = and_54_out ? and_54_out : 1'bz;  // Driver driver_29
  D_FF_AS d_ff_as_1 (.Set(1'b0), .D(and_51_out), .C(STB4), .Clr(IOT_IOF), .Q(IRQ_INHIBIT));  // open: nQ
  or or_8 (IRQ_BUS, FLAG_PRN, and_50_out, 1'b0, 1'b0, 1'b0);
  LED led_213 (.in(IRQ_BUS));
  or or_9 (or_9_out, IOT_IOF, RTF_IOF, IRQ_JMS, IOT_CAF, and_55_out);
  and and_56 (and_56_out, IOT_SRQ, CK4, FLAG_KBDIE, IRQ_BUS);
  D_FF_AS d_ff_as_2 (.Set(1'b0), .D(IRQ_INHIBIT), .C(STB4), .Clr(IOT_IOF), .Q(d_ff_as_2_q));  // open: nQ
  LED led_214 (.in(or_9_out));
  LED led_215 (.in(and_56_out));
  assign PC_CK = and_56_out ? and_56_out : 1'bz;  // Driver driver_30
  RS_FF_AS GIE (.S(d_ff_as_2_q), .R(or_9_out), .Q(FLAG_GIE));  // open: nQ
  LED led_216 (.in(FLAG_GIE));
  or or_10 (or_10_out, AND, L_GEN[10], ISZ, DCA, JMS);
  and and_57 (and_57_out, or_10_out, INDIRECT, CK1);
  and and_58 (and_58_out, INDIRECT, or_10_out, STB1);
  and and_59 (and_59_out, IRQ_BUS, FLAG_GIE);
  and and_60 (and_60_out, DIRECT, INIR2RAMA);
  and and_61 (and_61_out, ~DIRECT, INIR2RAMA);  // And
  LED led_217 (.in(and_57_out));
  LED led_218 (.in(and_58_out));
  LED led_219 (.in(and_59_out));
  assign IR2RAMA = and_57_out ? and_57_out : 1'bz;  // Driver driver_31
  assign RAMD2IND = and_57_out ? and_57_out : 1'bz;  // Driver driver_32
  assign RAM_OE = and_57_out ? and_57_out : 1'bz;  // Driver driver_33
  assign IND_CK = and_58_out ? and_58_out : 1'bz;  // Driver driver_34
  and and_62 (and_62_out, CK0, ~and_59_out);  // And
  and and_63 (and_63_out, CK0, and_59_out);
  assign IR2RAMA = and_60_out ? and_60_out : 1'bz;  // Driver driver_35
  assign IND2RAMA = and_61_out ? and_61_out : 1'bz;  // Driver driver_36
  and and_64 (and_64_out, IOT_GTF, CK5);
  and and_65 (and_65_out, IOT_GTF, STB5);
  // Probe on AC
  LED led_220 (.in(and_62_out));
  LED led_221 (.in(and_63_out));
  LED led_222 (.in(and_64_out));
  LED led_223 (.in(and_65_out));
  assign PC2ADDR = and_62_out ? and_62_out : 1'bz;  // Driver driver_37
  assign RAM_OE = and_62_out ? and_62_out : 1'bz;  // Driver driver_38
  assign IR_CK = and_62_out ? and_62_out : 1'bz;  // Driver driver_39
  assign PC_CK = and_62_out ? and_62_out : 1'bz;  // Driver driver_40
  assign IRQ_JMS = and_63_out ? and_63_out : 1'bz;  // Driver driver_41
  assign FORCE4000 = and_63_out ? and_63_out : 1'bz;  // Driver driver_42
  assign IR_CK = and_63_out ? and_63_out : 1'bz;  // Driver driver_43
  assign ROT2AC = and_64_out ? and_64_out : 1'bz;  // Driver driver_44
  assign CLA_KCC = and_64_out ? and_64_out : 1'bz;  // Driver driver_45
  assign OR_STATUS12 = and_64_out ? and_64_out : 1'bz;  // Driver driver_46
  assign AC_CK = and_65_out ? and_65_out : 1'bz;  // Driver driver_47
  and and_66 (and_66_out, or_10_out, L_GEN[1], CK3);
  and and_67 (and_67_out, or_10_out, L_GEN[1], STB3);
  and and_68 (and_68_out, or_10_out, L_GEN[1], CK1);
  LED led_224 (.in(and_68_out));
  and and_69 (and_69_out, or_10_out, L_GEN[1], STB1);
  LED led_225 (.in(and_69_out));
  and and_70 (and_70_out, or_10_out, L_GEN[1], CK2);
  LED led_226 (.in(and_70_out));
  and and_71 (and_71_out, or_10_out, L_GEN[1], STB2);
  LED led_227 (.in(and_71_out));
  LED led_228 (.in(and_66_out));
  LED led_229 (.in(and_67_out));
  and and_72 (RTF_IOF, IOT_RTF, CK1, ~AC[7]);  // And
  and and_73 (RTF_ION, IOT_RTF, CK1, AC[7]);
  and and_74 (and_74_out, IOT_RTF, CK4);
  and and_75 (and_75_out, IOT_RTF, STB4);
  and and_76 (RTF_LINK, IOT_RTF, AC[11]);
  assign IR2RAMA = and_68_out ? and_68_out : 1'bz;  // Driver driver_48
  assign RAM_OE = and_68_out ? and_68_out : 1'bz;  // Driver driver_49
  assign IND2INC = and_68_out ? and_68_out : 1'bz;  // Driver driver_50
  assign IND_CK = and_69_out ? and_69_out : 1'bz;  // Driver driver_51
  assign INC2RAMD = and_70_out ? and_70_out : 1'bz;  // Driver driver_52
  assign IND2INC = and_70_out ? and_70_out : 1'bz;  // Driver driver_53
  assign IR2RAMA = and_70_out ? and_70_out : 1'bz;  // Driver driver_54
  assign DAW[24] = and_71_out ? and_71_out : 1'bz;  // Driver driver_55
  assign IR2RAMA = and_66_out ? and_66_out : 1'bz;  // Driver driver_56
  assign RAMD2IND = and_66_out ? and_66_out : 1'bz;  // Driver driver_57
  assign RAM_OE = and_66_out ? and_66_out : 1'bz;  // Driver driver_58
  assign IND_CK = and_67_out ? and_67_out : 1'bz;  // Driver driver_59
  and and_77 (and_77_out, DIRECT, IN_IR2PC);
  and and_78 (and_78_out, ~DIRECT, IN_IR2PC);  // And
  LED led_230 (.in(RTF_IOF));
  LED led_231 (.in(RTF_ION));
  LED led_232 (.in(and_74_out));
  LED led_233 (.in(and_75_out));
  LED led_234 (.in(RTF_LINK));
  assign IR2PC = and_77_out ? and_77_out : 1'bz;  // Driver driver_60
  assign IND2PC = and_78_out ? and_78_out : 1'bz;  // Driver driver_61
  // Probe on {LINK, 1'b0, IRQ_BUS, IRQ_INHIBIT, FLAG_GIE, {7{1'b0}}}
  assign CLL = and_74_out ? and_74_out : 1'bz;  // Driver driver_62
  assign LINK_CK = and_75_out ? and_75_out : 1'bz;  // Driver driver_63
  and and_79 (and_79_out, AND, 1'b1, CK4);
  and and_80 (and_80_out, AND, 1'b1, STB4);
  and and_81 (and_81_out, AND, 1'b1, CK5);
  LED led_235 (.in(and_79_out));
  LED led_236 (.in(and_80_out));
  LED led_237 (.in(and_81_out));
  and and_82 (and_82_out, JMP, DIRECT, CK4);
  LED led_238 (.in(and_82_out));
  and and_83 (and_83_out, JMP, DIRECT, STB4);
  LED led_239 (.in(and_83_out));
  and and_84 (and_84_out, JMP, DIRECT, CK5);
  LED led_240 (.in(and_84_out));
  assign INIR2RAMA = and_79_out ? and_79_out : 1'bz;  // Driver driver_64
  assign RAMD2AC_AND = and_79_out ? and_79_out : 1'bz;  // Driver driver_65
  assign RAM_OE = and_79_out ? and_79_out : 1'bz;  // Driver driver_66
  assign AC_CK = and_80_out ? and_80_out : 1'bz;  // Driver driver_67
  assign DONE = and_81_out ? and_81_out : 1'bz;  // Driver driver_68
  Seven_Seg_Hex seven_seg_hex_20 (.d(CK_NUM), .dp(1'b0));
  assign IR2PC = and_82_out ? and_82_out : 1'bz;  // Driver driver_69
  assign PC_LD = and_82_out ? and_82_out : 1'bz;  // Driver driver_70
  assign PC_CK = and_83_out ? and_83_out : 1'bz;  // Driver driver_71
  assign DONE = and_84_out ? and_84_out : 1'bz;  // Driver driver_72
  // Probe on LATCHED_PC
  Keyboard KEYBOARD (.C(clk), .en(KEYBOARD_av), .D(KEYBOARD_d), .av(KEYBOARD_av));
  LED led_241 (.in(PH_FIRST));
  LED led_242 (.in(PH_STB));
  // Probe on KEYBOARD_d[11:0]
  or or_11 (or_11_out, IOT_KCF, IOT_KCC, IOT_KRB);
  and and_85 (and_85_out, IOT_KCC, CK4);
  and and_86 (and_86_out, IOT_KCC, STB4);
  and and_87 (and_87_out, IOT_KRB, CK4);
  and and_88 (and_88_out, IOT_KRB, STB4);
  LED led_243 (.in(PH_LAST));
  Register #(.Bits(12)) register_2 (.D(KEYBOARD_d[11:0]), .C(clk), .en(KEYBOARD_av), .Q(KBD12));
  RS_FF_AS KBD (.S(KEYBOARD_av), .R(or_11_out), .Q(FLAG_KBD));  // open: nQ
  LED led_244 (.in(or_11_out));
  LED led_245 (.in(and_85_out));
  assign ROT2AC = and_85_out ? and_85_out : 1'bz;  // Driver driver_73
  assign CLA_KCC = and_85_out ? and_85_out : 1'bz;  // Driver driver_74
  LED led_246 (.in(and_86_out));
  assign AC_CK = and_86_out ? and_86_out : 1'bz;  // Driver driver_75
  LED led_247 (.in(and_87_out));
  assign ROT2AC = and_87_out ? and_87_out : 1'bz;  // Driver driver_76
  assign OR_KBD12 = and_87_out ? and_87_out : 1'bz;  // Driver driver_77
  assign CLA_KCC = and_87_out ? and_87_out : 1'bz;  // Driver driver_78
  LED led_248 (.in(and_88_out));
  assign AC_CK = and_88_out ? and_88_out : 1'bz;  // Driver driver_79
  and and_89 (and_89_out, L_GEN[10], 1'b1, CK4);
  and and_90 (and_90_out, L_GEN[10], 1'b1, STB4);
  and and_91 (and_91_out, L_GEN[10], 1'b1, CK5);
  // Probe on KBD12
  LED led_249 (.in(FLAG_KBD));
  LED led_250 (.in(and_89_out));
  LED led_251 (.in(and_90_out));
  LED led_252 (.in(and_91_out));
  and and_92 (and_92_out, JMP, INDIRECT, CK4);
  LED led_253 (.in(and_92_out));
  and and_93 (and_93_out, JMP, INDIRECT, STB4);
  LED led_254 (.in(and_93_out));
  and and_94 (and_94_out, JMP, INDIRECT, CK5);
  LED led_255 (.in(and_94_out));
  assign INIR2RAMA = and_89_out ? and_89_out : 1'bz;  // Driver driver_80
  assign RAMD2AC_ADD = and_89_out ? and_89_out : 1'bz;  // Driver driver_81
  assign RAM_OE = and_89_out ? and_89_out : 1'bz;  // Driver driver_82
  assign AC_CK = and_90_out ? and_90_out : 1'bz;  // Driver driver_83
  assign LINK_CK = and_90_out ? and_90_out : 1'bz;  // Driver driver_84
  assign DONE = and_91_out ? and_91_out : 1'bz;  // Driver driver_85
  assign IR2RAMA = and_92_out ? and_92_out : 1'bz;  // Driver driver_86
  assign RAMD2PC = and_92_out ? and_92_out : 1'bz;  // Driver driver_87
  assign RAM_OE = and_92_out ? and_92_out : 1'bz;  // Driver driver_88
  assign PC_LD = and_92_out ? and_92_out : 1'bz;  // Driver driver_89
  assign PC_CK = and_93_out ? and_93_out : 1'bz;  // Driver driver_90
  assign DONE = and_94_out ? and_94_out : 1'bz;  // Driver driver_91
  Seven_Seg_Hex seven_seg_hex_21 (.d(CK_NUM), .dp(1'b0));
  // Probe on LATCHED_PC
  LED led_256 (.in(PH_FIRST));
  LED led_257 (.in(PH_STB));
  LED led_258 (.in(PH_LAST));
  and and_95 (and_95_out, IOT_KIE, AC[0]);
  and and_96 (and_96_out, IOT_KIE, ~AC[0]);  // And
  and and_97 (and_97_out, IOT_KSF, CK4, FLAG_KBD);
  and and_98 (and_98_out, IOT_KRS, CK4);
  and and_99 (and_99_out, IOT_KRS, STB4);
  LED led_259 (.in(LINK));
  // Probe on AC
  and and_100 (and_100_out, ISZ, 1'b1, CK4);
  LED led_260 (.in(and_100_out));
  and and_101 (and_101_out, ISZ, 1'b1, STB4);
  LED led_261 (.in(and_101_out));
  and and_102 (and_102_out, ISZ, 1'b1, CK5);
  LED led_262 (.in(and_102_out));
  and and_103 (and_103_out, ISZ, 1'b1, CK6);
  LED led_263 (.in(and_103_out));
  and and_104 (and_104_out, ISZ, 1'b1, INCZERO, CK7);
  LED led_264 (.in(and_104_out));
  and and_105 (and_105_out, ISZ, 1'b1, CK8);
  LED led_265 (.in(and_105_out));
  and and_106 (and_106_out, JMP, L_GEN[1], CK1);
  and and_107 (and_107_out, JMP, L_GEN[1], STB1);
  and and_108 (and_108_out, JMP, L_GEN[1], CK2);
  and and_109 (and_109_out, JMP, L_GEN[1], STB2);
  and and_110 (and_110_out, JMP, L_GEN[1], CK4);
  and and_111 (and_111_out, JMP, L_GEN[1], STB4);
  and and_112 (and_112_out, JMP, L_GEN[1], CK5);
  LED led_266 (.in(and_95_out));
  LED led_267 (.in(and_96_out));
  LED led_268 (.in(and_97_out));
  LED led_269 (.in(and_98_out));
  LED led_270 (.in(and_99_out));
  LED led_271 (.in(FLAG_GIE));
  assign INIR2RAMA = and_100_out ? and_100_out : 1'bz;  // Driver driver_92
  assign RAM_OE = and_100_out ? and_100_out : 1'bz;  // Driver driver_93
  assign INIR2RAMA = and_101_out ? and_101_out : 1'bz;  // Driver driver_94
  assign RAM_OE = and_101_out ? and_101_out : 1'bz;  // Driver driver_95
  assign DATA_CK = and_101_out ? and_101_out : 1'bz;  // Driver driver_96
  assign LD2INC = and_101_out ? and_101_out : 1'bz;  // Driver driver_97
  assign INIR2RAMA = and_102_out ? and_102_out : 1'bz;  // Driver driver_98
  assign DAW[24] = and_102_out ? and_102_out : 1'bz;  // Driver driver_99
  assign INC2RAMD = and_102_out ? and_102_out : 1'bz;  // Driver driver_100
  assign LD2INC = and_102_out ? and_102_out : 1'bz;  // Driver driver_101
  assign INIR2RAMA = and_103_out ? and_103_out : 1'bz;  // Driver driver_102
  assign RAM_OE = and_103_out ? and_103_out : 1'bz;  // Driver driver_103
  assign LD2INC = and_103_out ? and_103_out : 1'bz;  // Driver driver_104
  assign PC_CK = and_104_out ? and_104_out : 1'bz;  // Driver driver_105
  assign LD2INC = and_104_out ? and_104_out : 1'bz;  // Driver driver_106
  assign DONE = and_105_out ? and_105_out : 1'bz;  // Driver driver_107
  LED led_272 (.in(and_106_out));
  LED led_273 (.in(and_107_out));
  LED led_274 (.in(and_108_out));
  LED led_275 (.in(and_109_out));
  LED led_276 (.in(and_110_out));
  LED led_277 (.in(and_111_out));
  LED led_278 (.in(and_112_out));
  or or_12 (or_12_out, and_95_out, IOT_CAF);
  assign PC_CK = and_97_out ? and_97_out : 1'bz;  // Driver driver_108
  assign ROT2AC = and_98_out ? and_98_out : 1'bz;  // Driver driver_109
  assign OR_KBD12 = and_98_out ? and_98_out : 1'bz;  // Driver driver_110
  assign AC_CK = and_99_out ? and_99_out : 1'bz;  // Driver driver_111
  assign IR2RAMA = and_106_out ? and_106_out : 1'bz;  // Driver driver_112
  assign RAM_OE = and_106_out ? and_106_out : 1'bz;  // Driver driver_113
  assign IND2INC = and_106_out ? and_106_out : 1'bz;  // Driver driver_114
  assign IND_CK = and_107_out ? and_107_out : 1'bz;  // Driver driver_115
  assign INC2RAMD = and_108_out ? and_108_out : 1'bz;  // Driver driver_116
  assign IND2INC = and_108_out ? and_108_out : 1'bz;  // Driver driver_117
  assign IR2RAMA = and_108_out ? and_108_out : 1'bz;  // Driver driver_118
  assign DAW[24] = and_109_out ? and_109_out : 1'bz;  // Driver driver_119
  assign IR2RAMA = and_110_out ? and_110_out : 1'bz;  // Driver driver_120
  assign RAMD2PC = and_110_out ? and_110_out : 1'bz;  // Driver driver_121
  assign RAM_OE = and_110_out ? and_110_out : 1'bz;  // Driver driver_122
  assign PC_LD = and_110_out ? and_110_out : 1'bz;  // Driver driver_123
  assign PC_CK = and_111_out ? and_111_out : 1'bz;  // Driver driver_124
  assign DONE = and_112_out ? and_112_out : 1'bz;  // Driver driver_125
  RS_FF_AS KBD_IE (.S(or_12_out), .R(and_96_out), .Q(FLAG_KBDIE));  // open: nQ
  LED led_279 (.in(FLAG_KBDIE));
  and and_113 (and_113_out, DCA, 1'b1, CK4);
  and and_114 (and_114_out, DCA, 1'b1, STB4);
  and and_115 (and_115_out, DCA, 1'b1, CK5);
  and and_116 (and_116_out, OPR1, CK4);
  and and_117 (and_117_out, OPR1, STB4);
  and and_118 (and_118_out, OPR1, CK5);
  LED led_280 (.in(and_113_out));
  LED led_281 (.in(and_114_out));
  LED led_282 (.in(and_115_out));
  and and_119 (and_119_out, DCA, 1'b1, CK6);
  LED led_283 (.in(and_116_out));
  LED led_284 (.in(and_117_out));
  LED led_285 (.in(and_118_out));
  assign INIR2RAMA = and_113_out ? and_113_out : 1'bz;  // Driver driver_126
  assign AC2RAMD = and_113_out ? and_113_out : 1'bz;  // Driver driver_127
  assign DAW[24] = and_114_out ? and_114_out : 1'bz;  // Driver driver_128
  assign CLA = and_114_out ? and_114_out : 1'bz;  // Driver driver_129
  assign CLAx = and_115_out ? and_115_out : 1'bz;  // Driver driver_130
  assign ROT2AC = and_115_out ? and_115_out : 1'bz;  // Driver driver_131
  assign AC_CK = and_115_out ? and_115_out : 1'bz;  // Driver driver_132
  LED led_286 (.in(and_119_out));
  assign ROT2AC = and_116_out ? and_116_out : 1'bz;  // Driver driver_133
  assign LINK_CK = and_117_out ? and_117_out : 1'bz;  // Driver driver_134
  assign AC_CK = and_117_out ? and_117_out : 1'bz;  // Driver driver_135
  assign DONE = and_118_out ? and_118_out : 1'bz;  // Driver driver_136
  assign DONE = and_119_out ? and_119_out : 1'bz;  // Driver driver_137
  or or_13 (or_13_out, IOT_TPC, IOT_TLS);
  LED led_287 (.in(or_13_out));
  Terminal #(.termWidth(80), .termHeight(24)) PRINTER (.D({1'b0, AC[6:0]}), .C(or_13_out), .en(1'b1));
  and and_120 (and_120_out, OPR2, CK4);
  and and_121 (and_121_out, OPR2, SKIP, STB4);
  and and_122 (and_122_out, OPR2, CK5);
  and and_123 (and_123_out, OPR2, STB5);
  and and_124 (and_124_out, OPR2, CK6);
  Monoflop #(.timerDelay(50)) monoflop_1 (.C(or_13_out), .R(1'b0), .nQ(monoflop_1_nq));  // open: Q
  Monoflop #(.timerDelay(51)) monoflop_2 (.C(or_13_out), .R(1'b0), .Q(monoflop_2_q));  // open: nQ
  or or_14 (or_14_out, FLAG_PRN, FLAG_KBD);
  and and_125 (and_125_out, JMS, 1'b1, CK4);
  LED led_288 (.in(and_125_out));
  and and_126 (and_126_out, JMS, 1'b1, CK5);
  LED led_289 (.in(and_126_out));
  and and_127 (and_127_out, JMS, 1'b1, CK6);
  LED led_290 (.in(and_127_out));
  and and_128 (and_128_out, JMS, 1'b1, CK7);
  LED led_291 (.in(and_128_out));
  and and_129 (and_129_out, JMS, 1'b1, CK8);
  LED led_292 (.in(and_129_out));
  and and_130 (and_130_out, JMS, 1'b1, CK9);
  LED led_293 (.in(and_130_out));
  LED led_294 (.in(and_120_out));
  LED led_295 (.in(and_121_out));
  LED led_296 (.in(and_122_out));
  LED led_297 (.in(and_123_out));
  LED led_298 (.in(and_124_out));
  and and_131 (and_131_out, monoflop_1_nq, monoflop_2_q);
  or or_15 (or_15_out, and_131_out, IOT_TFL);
  or or_16 (or_16_out, IOT_TCF, IOT_CAF, IOT_TLS);
  and and_132 (and_132_out, IOT_TSF, CK4, FLAG_PRN);
  and and_133 (and_133_out, IOT_TSK, CK4, or_14_out);
  assign INIR2RAMA = and_125_out ? and_125_out : 1'bz;  // Driver driver_138
  assign PC2RAMD = and_125_out ? and_125_out : 1'bz;  // Driver driver_139
  assign INIR2RAMA = and_126_out ? and_126_out : 1'bz;  // Driver driver_140
  assign PC2RAMD = and_126_out ? and_126_out : 1'bz;  // Driver driver_141
  assign DAW[24] = and_126_out ? and_126_out : 1'bz;  // Driver driver_142
  assign PC_LD = and_126_out ? and_126_out : 1'bz;  // Driver driver_143
  assign IN_IR2PC = and_126_out ? and_126_out : 1'bz;  // Driver driver_144
  assign IN_IR2PC = and_127_out ? and_127_out : 1'bz;  // Driver driver_145
  assign PC_LD = and_127_out ? and_127_out : 1'bz;  // Driver driver_146
  assign PC_CK = and_127_out ? and_127_out : 1'bz;  // Driver driver_147
  assign IN_IR2PC = and_128_out ? and_128_out : 1'bz;  // Driver driver_148
  assign PC_LD = and_128_out ? and_128_out : 1'bz;  // Driver driver_149
  assign PC_CK = and_129_out ? and_129_out : 1'bz;  // Driver driver_150
  assign DONE = and_130_out ? and_130_out : 1'bz;  // Driver driver_151
  assign ROT2AC = and_120_out ? and_120_out : 1'bz;  // Driver driver_152
  assign PC_CK = and_121_out ? and_121_out : 1'bz;  // Driver driver_153
  assign ROT2AC = and_122_out ? and_122_out : 1'bz;  // Driver driver_154
  assign MQ_CK = and_122_out ? and_122_out : 1'bz;  // Driver driver_155
  assign AC_CK = and_123_out ? and_123_out : 1'bz;  // Driver driver_156
  assign DONE = and_124_out ? and_124_out : 1'bz;  // Driver driver_157
  LED led_299 (.in(or_15_out));
  LED led_300 (.in(or_16_out));
  LED led_301 (.in(and_132_out));
  LED led_302 (.in(and_133_out));
  RS_FF_AS PRN (.S(or_15_out), .R(or_16_out), .Q(FLAG_PRN));  // open: nQ
  assign PC_CK = and_132_out ? and_132_out : 1'bz;  // Driver driver_158
  assign PC_CK = and_133_out ? and_133_out : 1'bz;  // Driver driver_159
  LED led_303 (.in(FLAG_PRN));
  not not_13 (not_13_out, L_OPR3[9]);
  not not_14 (not_14_out, L_OPR3[9]);
  and and_134 (and_134_out, OPR3, 1'b1, CK4);
  and and_135 (and_135_out, OPR3, not_13_out, STB4);
  and and_136 (and_136_out, OPR3, CK5);
  and and_137 (and_137_out, OPR3, not_14_out, STB5);
  and and_138 (and_138_out, OPR3, CK6);
  and and_139 (and_139_out, OPR3, L_OPR3[9], STB4);
  LED led_304 (.in(and_134_out));
  LED led_305 (.in(and_135_out));
  LED led_306 (.in(and_136_out));
  LED led_307 (.in(and_137_out));
  LED led_308 (.in(and_138_out));
  LED led_309 (.in(and_139_out));
  assign ROT2AC = and_134_out ? and_134_out : 1'bz;  // Driver driver_160
  assign MQ_CK = and_135_out ? and_135_out : 1'bz;  // Driver driver_161
  assign ROT2AC = and_136_out ? and_136_out : 1'bz;  // Driver driver_162
  assign AC_CK = and_137_out ? and_137_out : 1'bz;  // Driver driver_163
  assign DONE = and_138_out ? and_138_out : 1'bz;  // Driver driver_164
  assign MQ_CK = and_139_out ? and_139_out : 1'bz;  // Driver driver_165
  assign AC_CK = and_139_out ? and_139_out : 1'bz;  // Driver driver_166
  Monoflop #(.timerDelay(2)) monoflop_3 (.C(CCC_I), .R(1'b0), .Q(monoflop_3_q));  // open: nQ
  Monoflop monoflop_4 (.C(CCC_R), .R(1'b0), .Q(monoflop_4_q));  // open: nQ
  Comparator #(.Bits(12)) comparator_1 (.a(BUS_PC), .b(12'h8a), .eq(comparator_1_eq));  // open: gt, lt
  and and_140 (CCC_BP1, comparator_1_eq, CK0);
  Comparator #(.Bits(32)) comparator_2 (.a(INSTCNT), .b(32'h8f0), .eq(CCC_BPI));  // open: gt, lt
  and and_141 (i_iac, OPR_IAC, 1'b1);
  and and_142 (i_cll, OPR_CLL, 1'b1);
  and and_143 (i_cma, OPR_CMA, 1'b1);
  and and_144 (i_cml, OPR_CML, 1'b1);
  and and_145 (i_osr, OPR_OSR, 1'b1);
  and and_146 (i_hlt, OPR_HLT, 1'b1);
  or or_17 (i_cla, L_OPR1[8], L_OPR2[9]);
  and and_147 (i_nop, L_OPR3[12], 1'b1);
  and and_148 (i_ral, OPR_LEFT, ~OPR_X2);  // And
  and and_149 (i_rar, OPR_RIGHT, ~OPR_X2);  // And
  and and_150 (i_rtl, OPR_LEFT, OPR_X2);
  and and_151 (i_rtr, OPR_RIGHT, OPR_X2);
  RS_FF_AS rs_ff_as_1 (.S(monoflop_4_q), .R(or_19_out), .Q(rs_ff_as_1_q));  // open: nQ
  or or_18 (or_18_out, monoflop_3_q, monoflop_4_q, rs_ff_as_1_q);
  PullDown pulldown_1 (.out(CCC_HLTCTRL));
  PullDown pulldown_2 (.out(CCC_BP2));
  PullDown pulldown_3 (.out(IR2PC));
  PullDown pulldown_4 (.out(IND2PC));
  PullDown pulldown_5 (.out(RAMD2PC));
  PullDown pulldown_6 (.out(ROT2AC));
  PullDown pulldown_7 (.out(RAMD2AC_ADD));
  PullDown pulldown_8 (.out(PC_LD));
  PullDown pulldown_9 (.out(IND2RAMA));
  PullDown pulldown_10 (.out(INC2RAMD));
  PullDown pulldown_11 (.out(PC2RAMD));
  PullDown pulldown_12 (.out(IR2RAMA));
  PullDown pulldown_13 (.out(IND2INC));
  PullDown pulldown_14 (.out(LD2INC));
  PullDown pulldown_15 (.out(RAMA_HOLD));
  PullDown pulldown_16 (.out(DATA_CK));
  PullDown pulldown_17 (.out(IR_CK));
  PullDown pulldown_18 (.out(PC_CK));
  PullDown pulldown_19 (.out(AC_CK));
  PullDown pulldown_20 (.out(IND_CK));
  PullDown pulldown_21 (.out(LINK_CK));
  PullDown pulldown_22 (.out(DAW[24]));
  PullDown pulldown_23 (.out(RAM_OE));
  PullDown pulldown_24 (.out(MQ_CK));
  LED led_310 (.in(or_18_out));
  or or_19 (or_19_out, CCC_H, CCC_HLTCTRL, CCC_BP2, CCC_BPICTRL);
  PullDown pulldown_25 (.out(CCC_BPICTRL));
  D_FF d_ff_1 (.D(or_22_out), .C(clk), .Q(d_ff_1_q));  // open: nQ
  LED led_311 (.in(or_19_out));
  and and_152 (i_snl, OPR_SNLSZL, ~OPR_TSTINV);  // And
  and and_153 (i_sza, OPR_SZASNA, ~OPR_TSTINV);  // And
  and and_154 (i_sma, OPR_SMASPA, ~OPR_TSTINV);  // And
  and and_155 (i_szl, OPR_SNLSZL, OPR_TSTINV);
  and and_156 (i_sna, OPR_SZASNA, OPR_TSTINV);
  and and_157 (i_spa, OPR_SMASPA, OPR_TSTINV);
  and and_158 (i_skp, ~OPR_SNLSZL, ~OPR_SZASNA, ~OPR_SMASPA, OPR_TSTINV);  // And
  RS_FF_AS rs_ff_as_2 (.S(or_18_out), .R(d_ff_1_q), .Q(rs_ff_as_2_q));  // open: nQ
  and and_159 (and_159_out, rs_ff_as_2_q, clk);
  or or_20 (or_20_out, BUS_IR[8], BUS_IR[7], BUS_IR[6]);
  LED led_312 (.in(and_159_out));
  LED led_313 (.in(IOT));
  or or_21 (or_21_out, CCC_S, and_159_out);
  LED led_314 (.in(or_21_out));
  Counter #(.Bits(5)) counter_1 (.en(1'b1), .C(or_21_out), .clr(or_22_out), .out(counter_1_out), .ovf(counter_1_ovf));
  LED led_315 (.in(or_22_out));
  // _74238 _74238_7: pin names not known; wires that end beside it: 1'b1, 1'b0, IOT, 1'b0, or_20_out, BUS_IR[3], BUS_IR[4], BUS_IR[5], L_DEVCPU, L_DEVHSR, L_DEVHSP, L_DEVKBD, L_DEVPRI, L_DEV5, L_DEV6, L_DEV7
  or or_22 (or_22_out, DONE, counter_1_ovf);
  PullDown pulldown_26 (.out(DONE));
  Add #(.Bits(5)) add_3 (.a(counter_1_out), .b(multiplexer_1_out), .c_i(1'b0), .s(add_3_s));  // open: c_o
  SEQUENCER sequencer_1 (
    .PH_FIRST(PH_FIRST), .PH_STB(PH_STB), .PH_LAST(PH_LAST),
    .STB_bits({STB9, STB8, STB7, STB6, STB5, STB4, STB3, STB2, STB1, STB0}),
    .CK_bits({CK9, CK8, CK7, CK6, CK5, CK4, CK3, CK2, CK1, CK0}), .CK_num(CK_NUM), .IN(add_3_s));
  Multiplexer #(.Bits(5), .Selector_Bits(2)) multiplexer_1 (
    .sel(2'b00), .in_0({5{1'b0}}), .in_1(5'b00001), .in_2(5'b00011), .in_3({5{1'b0}}), .out(multiplexer_1_out));
  // Probe STEP on CK_NUM
  // _74238 _74238_8: pin names not known; wires that end beside it: 1'b1, 1'b0, L_DEVCPU, 1'b0, 1'b0, BUS_IR[0], BUS_IR[1], BUS_IR[2], L_CPU[7], L_CPU[6], L_CPU[5], L_CPU[4], L_CPU[3], L_CPU[2], L_CPU[1], L_CAF
  // _74238 _74238_9: pin names not known; wires that end beside it: 1'b1, 1'b0, L_DEVKBD, 1'b0, 1'b0, BUS_IR[0], BUS_IR[1], BUS_IR[2], L_KBD[5], L_KBD[4], L_KBD[3], _74238_9_p12, L_KBD[2], L_KBD[1], L_KBD[0], _74238_9_p16, _74238_9_p12, _74238_9_p16
  // _74238 _74238_10: pin names not known; wires that end beside it: 1'b1, 1'b0, L_DEVPRI, 1'b0, 1'b0, BUS_IR[0], BUS_IR[1], BUS_IR[2], L_PRN[5], L_PRN[4], L_PRN[3], _74238_10_p12, L_PRN[2], L_PRN[1], L_PRN[0], _74238_10_p16, _74238_10_p12, _74238_10_p16

  // Other names for the same wires on the sheet: RAMADDR[11:0] = DAW[23:12]; AC0[2:0] = AC[2:0]; AC1[2:0] = AC[5:3];
  //   AC2[2:0] = AC[8:6]; AC3[2:0] = AC[11:9]; L_GEN (some bits) = {AND, ISZ, DCA, JMS, JMP, IOT, DIRECT, INDIRECT};
  //   IR0[2:0] = BUS_IR[2:0]; IR1[2:0] = BUS_IR[5:3]; IR2[2:0] = BUS_IR[8:6]; IR3[2:0] = BUS_IR[11:9];
  //   PC0[2:0] = BUS_PC[2:0]; PC1[2:0] = BUS_PC[5:3]; PC2[2:0] = BUS_PC[8:6]; PC3[2:0] = BUS_PC[11:9];
  //   L_IRQ[4:0] = {FLAG_GIE, IRQ_BUS, FLAG_KBDIE, FLAG_KBD, FLAG_PRN};
  //   STATUS12 (some bits) = {LINK, IRQ_BUS, IRQ_INHIBIT, FLAG_GIE};
  //   L_OPR1 (some bits) = {i_nop, i_cll, i_cma, i_cml, i_iac, i_rar, i_rtr, i_ral, i_rtl};
  //   L_OPR2[8:0] = {i_skp, i_sma, i_sza, i_spa, i_sna, i_snl, i_szl, i_osr, i_hlt}; L_CPU[0] = L_CAF;
  //   L_GTF = L_CPU[3]; L_IOF = L_CPU[5]; L_ION = L_CPU[6]; L_KCC = L_KBD[3]; L_KCF = L_KBD[5]; L_KIE = L_KBD[1];
  //   L_KRB = L_KBD[0]; L_KRS = L_KBD[2]; L_KSF = L_KBD[4]; L_RTF = L_CPU[2]; L_SGT = L_CPU[1]; L_SKON = L_CPU[7];
  //   L_SRQ = L_CPU[4]; L_TCF = L_PRN[3]; L_TFL = L_PRN[5]; L_TLS = L_PRN[0]; L_TPC = L_PRN[2]; L_TSF = L_PRN[4];
  //   L_TSK = L_PRN[1]; MP = L_GEN[0]; MQ0[2:0] = MQ[2:0]; MQ1[2:0] = MQ[5:3]; MQ2[2:0] = MQ[8:6];
  //   MQ3[2:0] = MQ[11:9]; OPR = L_GEN[4]; OPR_ASL = L_OPR3[5]; OPR_CLA1 = L_OPR1[8]; OPR_CLA2 = L_OPR2[9];
  //   OPR_CLA3 = L_OPR3[11]; OPR_DVI = L_OPR3[2]; OPR_LSR = L_OPR3[6]; OPR_MQA = L_OPR3[8]; OPR_MQL = L_OPR3[7];
  //   OPR_MUY = L_OPR3[1]; OPR_NMI = L_OPR3[3]; OPR_NOP = L_OPR3[12]; OPR_SCA = L_OPR3[10]; OPR_SCL = L_OPR3[0];
  //   OPR_SHL = L_OPR3[4]; OPR_SWP = L_OPR3[9]; plus__plus_INDIRECT = L_GEN[1]; RAM_WE = DAW[24];
  //   RAMDATA[11:0] = DAW[11:0]; TAD = L_GEN[10]; XTAL = clk

  // Notes on the sheet:
  //   clk: Hz: 50000
  //   IR DECODER
  //   CP=0 PAGE ZERO
  //   CP=1 CURRENT PAGE
  //   IA=0 DIRECT
  //   IA=1 INDIRECT
  //   SEQ OPR 1 MICROCODES
  //   ------------------------------------
  //   1 CLA CLL
  //   2 CMA CML
  //   3 IAC
  //   4 RAR RAL RTR RTL BSW
  //   github.com/SmallRoomLabs/PDP8-X
  //   PC
  //   IR
  //   AC
  //   MQ
  //   ACCUMULATOR
  //   PDP-8/X r3
  //   LINK
  //   C
  //   000 printhelp.bin                PC:0200 (This)
  //   001 D0AB-InstTest-1.pt           PC:0200 SR:7777 Watch:0121 cont@0147
  //   002 D0BB-InstTest-2.pt           PC:0200 SR:xxxx Watch:3747
  //   003 D0IB-JMPJMS.pt               PC:0200 SR:xxxx Watch:3571
  //   004 D0JB-JMPJMS-RANDOM.pt        PC:0200 SR:0000 Watch:0044
  //   005 D0DB-RandomAND.pt            PC:0200 SR:0000 Watch:0202
  //   006 D0EB-Random-TAD.pt           PC:0200 SR:0000 Watch:6776
  //   007 D0FC-Random-ISZ.pt           PC:0200 SR:0000 Watch:0175
  //   010 D0GC-Random-DCA.pt           PC:0200 SR:0000 Watch 0006/0011
  //   011 D0CC-AddTest.pt              PC:0200 
  //   012 D1AA-Memory-Checkerboard.pt  PC:0200 
  //   013 D1EA-Memory-Address.rim      PC:0200 
  //   014 FOCAL-8.bn                   PC:0200 
  //   015 FOCAL-8-NOINT.bn             PC:0200 
  //   016 myfocal
  //   <end>
  //   OPR-3
  //   NOP
  //   OPR-2
  //   CLA
  //   OPR-1
  //   OPCODES
  //   AND
  //   -
  //   TAD
  //   1 pcs 7404 Hex inverter
  //   1 pcs 7408 Quad 2-input AND
  //   1 pcs 7411 Triple 3-input AND
  //   2 pcs 7427 Triple 3-input NOR
  //   1 pcs 74238 Decoder 3-to-8
  //   SKP
  //   LATCHED PC
  //   SCA
  //   SMA
  //   CLL
  //   ISZ
  //   SWP
  //   MQA
  //   SZA
  //   SPA
  //   CMA
  //   CML
  //   DCA
  //   JMS
  //   F
  //   S
  //   MQL
  //   SNA
  //   IAC
  //   JMP
  //   L
  //   LSR
  //   SNL
  //   RAR
  //   IOT
  //   ASL
  //   SHL
  //   OSR
  //   SZL
  //   RTR
  //   RAL
  //   OPR
  //   DIR
  //   IOT DECODER
  //   NMI
  //   HLT
  //   RTL
  //   IND
  //   CPU COMMAND & CONTROL
  //   ROM BANK
  //   DVI
  //   AUTO
  //   IND
  //   STATE
  //   INSTR.
  //   RUN
  //   HALT
  //   PC=0200
  //   MUY
  //   SCL
  //   CURR
  //   PAGE
  //   BREAKPOINT - PC
  //   BREAKPOINT - INSTR. CNT
  //   600x
  //   CPU FLAGS & 
  //   INTERRUPT
  //   603x
  //   TTY KEYBOARD
  //   SLOW READER
  //   604x
  //   TTY PRINTER
  //   SLOW PUNCH
  //   IOT-PRINTER
  //   TFL
  //   IOT-KEYBOARD
  //   KCF
  //   IOT-CPU
  //   SKON
  //   INTERRUPT FLAGS
  //   GIE
  //   SWITCHES
  //   ROTATES
  //   TSF
  //   KSF
  //   ION
  //   IRQ
  //   BUS
  //   TCF
  //   KCC
  //   IOF
  //   TTY
  //   IE
  //   TPC
  //   TSK
  //   KRS
  //   KIE
  //   SRQ
  //   GTF
  //   PRN
  //   KBD
  //   TLS
  //   KRB
  //   RTF
  //   SGT
  //   CAF
  //   OPR DECODER
  //   OPR1
  //   OPR2
  //   OPR3
  //   SEQ OPR 2 MICROCODES
  //   ------------------------------------
  //   1 SMA SPA SZA SZN SNK SZL SKP
  //   2 CLA
  //   3 OSR
  //   4 HLT
  //   PCIN
  //   SKIP LOGIC
  //   AC=0
  //   AC negative
  //   LINK<>0
  //   PCOUT
  //   SMA      7500  skip on minus AC
  //   SPA      7510  skip on plus AC
  //   SZA      7440  skip on zero AC
  //   SNA      7450  skip on non-zero AC
  //   SNL      7420  skip on non-zero link
  //   SZL      7430  skip on zero link
  //   MAIN DATA-PATHS
  //   RAMADDR
  //   contents of eeprom_1 (hex, n*v repeats v):
  //   f02,f02,f02,f02,f02,f02,f02,f02,90,f02,f02,f02,f02,f02,f02,f02,f02,f02,f02,f02,f02,
  //   f02,f02,f02,f02,f02,f02,f02,f02,f02,f02,f02,f02,f02,f02,f02,f02,f02,f02,f02,f02,f02,
  //   f02,f02,f02,f02,f02,f02,f02,f02,f02,f02,f02,f02,f02,f02,f02,f02,f02,f02,f02,f02,f02,
  //   f02,e00,e00,c02,e00,e00,c01,e00,e00,c04,e00,e00,c02,e00,e00,c05,e00,e00,e00,e00,a54,
  //   e00,e00,a40,f02,f02,f02,f02,f02,f02,f02,f02,f02,f02,f02,f02,f02,f02,f02,f02,f02,f02,
  //   f02,f02,f02,f02,f02,f02,f02,f02,f02,f02,f02,f02,f02,f02,f02,f02,f02,f02,f02,f02,f02,
  //   f02,f02,e00,309,209,309,209,c20,e80,308,f28,a40,88c,a86,0,c21,a8d,c26,b8c,a,a,c1,
  //   f6,e1,e9,ec,e1,e2,ec,e5,a0,f3,ef,e6,f4,f7,e1,f2,e5,f3,ba,a,ad,ad,ad,ad,ad,ad,ad,ad,
  //   ad,ad,ad,ad,ad,ad,ad,ad,ad,ad,ad,ad,a,30,30,30,3a,20,70,72,69,6e,74,68,65,6c,70,2e,
  //   62,69,6e,20,20,20,20,20,20,20,20,20,20,20,20,20,20,20,20,50,43,3a,30,32,30,30,20,
  //   28,54,68,69,73,20,68,65,6c,70,29,d,30,30,31,3a,20,44,30,41,42,2d,49,6e,73,74,54,65,
  //   73,74,2d,31,2e,70,74,20,20,20,20,20,20,20,20,20,20,20,50,43,3a,30,32,30,30,20,53,
  //   52,3a,37,37,37,37,20,57,61,74,63,68,3a,30,31,32,31,20,63,6f,6e,74,40,30,31,34,37,
  //   d,30,30,32,3a,20,44,30,42,42,2d,49,6e,73,74,54,65,73,74,2d,32,2e,70,74,20,20,20,20,
  //   20,20,20,20,20,20,20,50,43,3a,30,32,30,30,20,53,52,3a,78,78,78,78,20,57,61,74,63,
  //   68,3a,33,37,34,37,d,30,30,33,3a,20,44,30,49,42,2d,4a,4d,50,4a,4d,53,2e,70,74,20,20,
  //   20,20,20,20,20,20,20,20,20,20,20,20,20,50,43,3a,30,32,30,30,20,53,52,3a,78,78,78,
  //   78,20,57,61,74,63,68,3a,33,35,37,31,d,30,30,34,3a,20,44,30,4a,42,2d,4a,4d,50,4a,4d,
  //   53,2d,52,41,4e,44,4f,4d,2e,70,74,20,20,20,20,20,20,20,20,50,43,3a,30,32,30,30,20,
  //   53,52,3a,30,30,30,30,20,57,61,74,63,68,3a,30,30,34,34,d,30,30,35,3a,20,44,30,44,42,
  //   2d,52,61,6e,64,6f,6d,41,4e,44,2e,70,74,20,20,20,20,20,20,20,20,20,20,20,20,50,43,
  //   3a,30,32,30,30,20,53,52,3a,30,30,30,30,20,57,61,74,63,68,3a,30,32,30,32,d,30,30,36,
  //   3a,20,44,30,45,42,2d,52,61,6e,64,6f,6d,2d,54,41,44,2e,70,74,20,20,20,20,20,20,20,
  //   20,20,20,20,50,43,3a,30,32,30,30,20,53,52,3a,30,30,30,30,20,57,61,74,63,68,3a,36,
  //   37,37,36,d,30,30,37,3a,20,44,30,46,43,2d,52,61,6e,64,6f,6d,2d,49,53,5a,2e,70,74,20,
  //   20,20,20,20,20,20,20,20,20,20,50,43,3a,30,32,30,30,20,53,52,3a,30,30,30,30,20,57,
  //   61,74,63,68,3a,30,31,37,35,d,30,31,30,3a,20,44,30,47,43,2d,52,61,6e,64,6f,6d,2d,44,
  //   43,41,2e,70,74,20,20,20,20,20,20,20,20,20,20,20,50,43,3a,30,32,30,30,20,53,52,3a,
  //   30,30,30,30,20,57,61,74,63,68,20,30,30,30,36,2f,30,30,31,31,d,30,31,31,3a,20,44,30,
  //   43,43,2d,41,64,64,54,65,73,74,2e,70,74,20,20,20,20,20,20,20,20,20,20,20,20,20,20,
  //   50,43,3a,30,32,30,30,20,d,30,31,32,3a,20,44,31,41,41,2d,4d,65,6d,6f,72,79,2d,43,68,
  //   65,63,6b,65,72,62,6f,61,72,64,2e,70,74,20,20,50,43,3a,30,32,30,30,20,d,30,31,33,3a,
  //   20,44,31,45,41,2d,4d,65,6d,6f,72,79,2d,41,64,64,72,65,73,73,2e,72,69,6d,20,20,20,
  //   20,20,20,50,43,3a,30,32,30,30,20,d,30,31,34,3a,20,46,4f,43,41,4c,2d,38,2e,62,6e,20,
  //   20,20,20,20,20,20,20,20,20,20,20,20,20,20,20,20,20,20,50,43,3a,30,32,30,30,20,d,30,
  //   31,35,3a,20,46,4f,43,41,4c,2d,38,2d,4e,4f,49,4e,54,2e,62,6e,20,20,20,20,20,20,20,
  //   20,20,20,20,20,20,50,43,3a,30,32,30,30,20,d,30,31,36,3a,20,6d,79,66,6f,63,61,6c,2e,
  //   62,69,6e,d,bc,e5,ee,e4,be,d,0,f02,f02,f02,f02,f02,f02,f02,f02,f02,f02,f02,f02,f02,
  //   f02,f02,f02,f02,f02,f02,f02,f02,f02,f02,f02,f02,f02,f02,f02,f02,f02,f02,f02,f02,f02,
  //   f02,f02,f02,f02,f02,f02,f02,f02,f02,f02,f02,f02,f02,f02,f02,f02,f02,f02,f02,f02,f02,
  //   f02,f02,f02,f02,f02,f02,f02,f02,f02,f02,f02,f02,f02,f02,f02,f02,f02,f02,f02,f02,f02,
  //   f02,f02,f02,f02,f02,f02,f02,f02,f02,f02,f02,f02,f02,f02,f02,f02,f02,f02,f02,f02,f02,
  //   f02,f02,f02,f02,f02,f02,f02,f02,f02,f02,f02,f02,f02,f02,f02,f02,f02,f02,f02,f02,f02,
  //   f02,f02,f02,f02,f02,f02,f02,f02,f02,f02,f02,f02,f02,f02,f02,f02,f02,f02,f02,f02,f02,
  //   f02,f02,f02,f02,f02,f02,f02,f02,f02,f02,f02,f02,f02,f02,f02,f02,f02,f02,f02,f02,f02,
  //   f02,f02,f02,f02,f02,f02,f02,f02,f02,f02,f02,f02,f02,f02,f02,f02,f02,f02,f02,f02,f02,
  //   f02,f02,f02,f02,f02,f02,f02,f02,f02,f02,f02,f02,f02,f02,f02,f02,f02,f02,f02,f02,f02,
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  //   RAMDATA
  //   DATA
  //   1 pcs 7404 Hex inverter
  //   7 pcs 7408 Quad 2-input AND
  //   1 pcs 7411 Triple 3-input AND
  //   1 pcs 8-input NOR (***REPLACE***)
  //   1 pcs 74238 Decoder 3-to-8
  //   INDOUT
  //   600x - INTERRUPT INSTRUCTIONS
  //   LATCHED
  //   DATA
  //   Turn interrupt ON
  //   Turn interrupt OFF
  //   Clear All Flags
  //   Skip if interrupt ON, and turn OFF
  //   Skip interrupt request
  //   External IRQ
  //   sources
  //   INC
  //   IND
  //   STEP1
  //   IND
  //   STEP2
  //   Get interrupt flags
  //   FETCH OP &
  //   INCREMENT PC
  //   FORCE 4000 (JMS 0)
  //   TO IR AS INTERRUPT
  //   Skip on Greater Than flag
  //   Restore interrupt flags
  //   iAuto 1
  //   iAuto 2
  //   iAuto 3
  //   iAuto 4
  //   603x - IOT Keyboard
  //   Prepare to set
  //   new PC
  //   Actually set
  //   new PC
  //   Keyboard Clear Flags
  //   Keyboard and AC Clear
  //   Keyboard Read and 
  //   Begin next read
  //   TAD
  //   STEP1
  //   TAD
  //   STEP2
  //   Prepare to set PC
  //   with new vector
  //   JMP i
  //   Keyboard Interrupt Enable
  //   Keyboard Skip if Flag
  //   Keyboard Read Static
  //   AUTOINDEX
  //   Save value
  //   from IND
  //   indo LATDAT
  //   JMP i-auto
  //   SKIP IF
  //   AC=ZERO
  //   OPR 1
  //   604x - IOT Printer
  //   Teleprinter Print Character
  //   Teleprinter Load and Start
  //   Teleprinter Flag set (aka SPF)
  //   Teleprinter Clear Flag
  //   Teleprinter Skip if Flag
  //   Teleprinter Skip (aka SPI)
  //   OPR 2
  //   Prepate to store 
  //   return addr
  //   to [ind]
  //   Store return addr
  //   to [ind]
  //   Actually increment
  //   PC
  //   Pause to accept
  //   new PC inc clk
  //   OPR_SWP
  //   OPR 3
  //   CLOCK CYCLE CONTROLLER
  //   CONNECTORS & DECODERS FOR LED/DISPLAYS
  //   PC 
  //   BREAKPOINT
  //   INSTRUCTION
  //   INST COUNT
  //   BREAKPOINT
  //   [LED] IOT DECODER
  //   Keyboard Clear and read Character
  //   Keyboard Read and Begin next read
endmodule
